// Logisim project logisim_lab_newest.circ as structural Verilog: 12 circuits, main circuit main
module main (
);

  wire alucontrolcircuit_1_alu_src, and_1_out, clock_1_out, comparator_1_eq, main_control_circuit_1_branch,
       main_control_circuit_1_memread, main_control_circuit_1_memtoreg, main_control_circuit_1_memwrite,
       main_control_circuit_1_regwrite;
  wire [3:0] alucontrolcircuit_1_alu_ctrl0;
  wire [31:0] adder_1_out, adder_2_out, bitregister32_1_rdata1, bitregister32_1_rdata2, dram64mx32byte_1_p6,
       immgen_1_imm32, instructionmemory_1_instruction, multiplexer_1_out, multiplexer_2_out,
       multiplexer_3_out, register_1_q, thirty_two_bit_alu_1_r;

  Register #(.width(32)) register_1 (
    .D(multiplexer_2_out), .en(1'b1), .clk(clock_1_out), .Q(register_1_q));  // open: clr
  Clock clock_1 (.out(clock_1_out));
  Adder #(.width(32)) adder_1 (.a(register_1_q), .b(32'h4), .out(adder_1_out));  // open: cin, cout
  InstructionMemory instructionmemory_1 (
    .Address(register_1_q[25:0]), .Clock_in(clock_1_out), .Instruction(instructionmemory_1_instruction));
  main_control_circuit main_control_circuit_1 (
    .I6_0(instructionmemory_1_instruction[6:0]), .MemtoReg(main_control_circuit_1_memtoreg),
    .RegWrite(main_control_circuit_1_regwrite), .MemRead(main_control_circuit_1_memread),
    .MemWrite(main_control_circuit_1_memwrite), .Branch(main_control_circuit_1_branch));
  BitRegister32 bitregister32_1 (
    .WData(multiplexer_3_out), .Write(main_control_circuit_1_regwrite),
    .RReg1(instructionmemory_1_instruction[11:7]), .WReg(instructionmemory_1_instruction[21:17]),
    .RReg2(instructionmemory_1_instruction[16:12]), .Clock_in(clock_1_out), .RData1(bitregister32_1_rdata1),
    .RData2(bitregister32_1_rdata2));
  ImmGen immgen_1 (.Instruction(instructionmemory_1_instruction), .Imm32(immgen_1_imm32));
  ALUControlCircuit alucontrolcircuit_1 (
    .I30(instructionmemory_1_instruction[30]), .I14(instructionmemory_1_instruction[14]),
    .I13(instructionmemory_1_instruction[13]), .I12(instructionmemory_1_instruction[12]),
    .I5(instructionmemory_1_instruction[5]), .I4(instructionmemory_1_instruction[4]),
    .ALU_Ctrl3(alucontrolcircuit_1_alu_ctrl0[3]), .ALU_Ctrl2(alucontrolcircuit_1_alu_ctrl0[2]),
    .ALU_Ctrl1(alucontrolcircuit_1_alu_ctrl0[1]), .ALU_Ctrl0(alucontrolcircuit_1_alu_ctrl0[0]),
    .ALU_Src(alucontrolcircuit_1_alu_src));
  Multiplexer #(.width(32)) multiplexer_1 (
    .in0(bitregister32_1_rdata2), .in1(immgen_1_imm32), .out(multiplexer_1_out),
    .sel(alucontrolcircuit_1_alu_src));
  Adder #(.width(32)) adder_2 (.a(register_1_q), .b(immgen_1_imm32), .out(adder_2_out));  // open: cin, cout
  Comparator #(.width(32)) comparator_1 (
    .a(bitregister32_1_rdata1), .b(bitregister32_1_rdata2), .eq(comparator_1_eq));  // open: gt, lt
  thirty_two_bit_ALU thirty_two_bit_alu_1 (
    .ALU_Ctrl(alucontrolcircuit_1_alu_ctrl0), .A(bitregister32_1_rdata1), .B(multiplexer_1_out),
    .R(thirty_two_bit_alu_1_r));  // open: C_in, C_out
  and and_1 (and_1_out, main_control_circuit_1_branch, comparator_1_eq);
  Multiplexer #(.width(32)) multiplexer_2 (
    .in0(adder_1_out), .in1(adder_2_out), .out(multiplexer_2_out), .sel(and_1_out));
  // DRAM64Mx32Byte dram64mx32byte_1: pin names not known; wires that end beside it: clock_1_out, main_control_circuit_1_memread, main_control_circuit_1_memwrite, thirty_two_bit_alu_1_r, bitregister32_1_rdata2, dram64mx32byte_1_p6
  Multiplexer #(.width(32)) multiplexer_3 (
    .in0(thirty_two_bit_alu_1_r), .in1(dram64mx32byte_1_p6), .out(multiplexer_3_out),
    .sel(main_control_circuit_1_memtoreg));
endmodule

module ALUControlCircuit (
  input  I30,
  input  I14,
  input  I13,
  input  I12,
  input  I5,
  input  I4,
  output ALU_Ctrl3,
  output ALU_Ctrl2,
  output ALU_Ctrl1,
  output ALU_Ctrl0,
  output ALU_Src
);

  wire and_2_out, not_1_out, not_2_out, not_3_out, not_4_out, not_5_out;

  not not_1 (not_1_out, I14);
  not not_2 (not_2_out, I13);
  not not_3 (not_3_out, I12);
  not not_4 (not_4_out, I5);
  not not_5 (not_5_out, I4);
  and and_1 (ALU_Ctrl2, I30, not_2_out, I5);
  or or_1 (ALU_Ctrl1, not_2_out, not_5_out);
  or or_2 (ALU_Ctrl0, not_1_out, and_2_out);
  and and_2 (and_2_out, I13, not_3_out);
  or or_3 (ALU_Src, not_4_out, not_5_out);

  assign ALU_Ctrl3 = 1'b0;
endmodule

module ImmGen (
  input  [31:0] Instruction,
  output [31:0] Imm32
);

  Multiplexer #(.width(4)) multiplexer_1 (
    .in0(Instruction[24:21]), .in1(Instruction[11:8]), .out(Imm32[4:1]), .sel(Instruction[5]));
  Multiplexer multiplexer_2 (.in0(Instruction[31]), .in1(Instruction[7]), .out(Imm32[11]), .sel(Instruction[6]));
  Multiplexer #(.select(2)) multiplexer_3 (
    .in0(Instruction[20]), .in1(Instruction[7]), .in3(1'b0), .out(Imm32[0]), .sel(Instruction[6:5]));  // open: in2
  assign Imm32[31:12] = {{19{Instruction[31]}}, Instruction[31]};  // Bit_Extender bit_extender_1

  assign Imm32[10:5] = Instruction[30:25];

  // Other names for the same wires on the sheet: I30_25[5:0] = Instruction[30:25]; I5 = Instruction[5];
  //   I6_5[1:0] = Instruction[6:5]; I6 = Instruction[6]; I7 = Instruction[7]; I11_8[3:0] = Instruction[11:8];
  //   I20 = Instruction[20]; I24_21[3:0] = Instruction[24:21]; I31 = Instruction[31]
endmodule

module InstructionMemory (
  input  [25:0] Address,
  input  Clock_in,
  output [31:0] Instruction
);

  wire not_1_out;

  not not_1 (not_1_out, Clock_in);
  RAM #(.addrWidth(24), .asyncread("true"), .dataWidth(32)) ram_1 (
    .addr(Address[25:2]), .oe(not_1_out), .dout(Instruction));  // open: we, clk, din
endmodule

module one_bit_adder (
  input  A,
  input  B,
  input  C_in,
  output S,
  output C_out
);

  wire and_1_out, and_2_out, xor_1_out;

  xor xor_1 (xor_1_out, A, B);
  and and_1 (and_1_out, xor_1_out, C_in);
  and and_2 (and_2_out, A, B);
  xor xor_2 (S, xor_1_out, C_in);
  or or_1 (C_out, and_1_out, and_2_out);
endmodule

module one_bit_ALU (
  input  [3:0] ALU_Ctrl,
  input  A,
  input  B,
  input  C_in,
  output R,
  output C_out
);

  wire and_1_out, multiplexer_1_out, not_1_out, one_bit_adder_1_s, or_1_out, xor_1_out;

  not not_1 (not_1_out, B);
  Multiplexer multiplexer_1 (.in0(B), .in1(not_1_out), .out(multiplexer_1_out), .sel(ALU_Ctrl[2]));
  and and_1 (and_1_out, A, multiplexer_1_out);
  or or_1 (or_1_out, A, multiplexer_1_out);
  xor xor_1 (xor_1_out, A, multiplexer_1_out);
  one_bit_adder one_bit_adder_1 (.A(A), .B(multiplexer_1_out), .C_in(C_in), .S(one_bit_adder_1_s), .C_out(C_out));
  Multiplexer #(.select(2)) multiplexer_2 (
    .in0(and_1_out), .in1(or_1_out), .in2(xor_1_out), .in3(one_bit_adder_1_s), .out(R), .sel(ALU_Ctrl[1:0]));
endmodule

module four_bit_ALU (
  input  [3:0] Ctrl,
  input  C_in,
  input  [3:0] A,
  input  [3:0] B,
  output [3:0] R,
  output C_out
);

  wire one_bit_alu_1_c_out, one_bit_alu_2_c_out, one_bit_alu_3_c_out;

  one_bit_ALU one_bit_alu_1 (.ALU_Ctrl(Ctrl), .A(A[0]), .B(B[0]), .C_in(C_in), .R(R[0]), .C_out(one_bit_alu_1_c_out));
  one_bit_ALU one_bit_alu_2 (
    .ALU_Ctrl(Ctrl), .A(A[1]), .B(B[1]), .C_in(one_bit_alu_1_c_out), .R(R[1]), .C_out(one_bit_alu_2_c_out));
  one_bit_ALU one_bit_alu_3 (
    .ALU_Ctrl(Ctrl), .A(A[2]), .B(B[2]), .C_in(one_bit_alu_2_c_out), .R(R[2]), .C_out(one_bit_alu_3_c_out));
  one_bit_ALU one_bit_alu_4 (.ALU_Ctrl(Ctrl), .A(A[3]), .B(B[3]), .C_in(one_bit_alu_3_c_out), .R(R[3]), .C_out(C_out));
endmodule

module thirty_two_bit_ALU (
  input  [3:0] ALU_Ctrl,
  input  C_in,
  input  [31:0] A,
  input  [31:0] B,
  output [31:0] R,
  output C_out
);

  wire four_bit_alu_1_c_out, four_bit_alu_2_c_out, four_bit_alu_3_c_out, four_bit_alu_4_c_out,
       four_bit_alu_5_c_out, four_bit_alu_6_c_out, four_bit_alu_7_c_out;

  four_bit_ALU four_bit_alu_1 (
    .Ctrl(ALU_Ctrl), .C_in(C_in), .A(A[3:0]), .B(B[3:0]), .R(R[3:0]), .C_out(four_bit_alu_1_c_out));
  four_bit_ALU four_bit_alu_2 (
    .Ctrl(ALU_Ctrl), .C_in(four_bit_alu_1_c_out), .A(A[7:4]), .B(B[7:4]), .R(R[7:4]),
    .C_out(four_bit_alu_2_c_out));
  four_bit_ALU four_bit_alu_3 (
    .Ctrl(ALU_Ctrl), .C_in(four_bit_alu_2_c_out), .A(A[11:8]), .B(B[11:8]), .R(R[11:8]),
    .C_out(four_bit_alu_3_c_out));
  four_bit_ALU four_bit_alu_4 (
    .Ctrl(ALU_Ctrl), .C_in(four_bit_alu_3_c_out), .A(A[15:12]), .B(B[15:12]), .R(R[15:12]),
    .C_out(four_bit_alu_4_c_out));
  four_bit_ALU four_bit_alu_5 (
    .Ctrl(ALU_Ctrl), .C_in(four_bit_alu_4_c_out), .A(A[19:16]), .B(B[19:16]), .R(R[19:16]),
    .C_out(four_bit_alu_5_c_out));
  four_bit_ALU four_bit_alu_6 (
    .Ctrl(ALU_Ctrl), .C_in(four_bit_alu_5_c_out), .A(A[23:20]), .B(B[23:20]), .R(R[23:20]),
    .C_out(four_bit_alu_6_c_out));
  four_bit_ALU four_bit_alu_7 (
    .Ctrl(ALU_Ctrl), .C_in(four_bit_alu_6_c_out), .A(A[27:24]), .B(B[27:24]), .R(R[27:24]),
    .C_out(four_bit_alu_7_c_out));
  four_bit_ALU four_bit_alu_8 (
    .Ctrl(ALU_Ctrl), .C_in(four_bit_alu_7_c_out), .A(A[31:28]), .B(B[31:28]), .R(R[31:28]), .C_out(C_out));
endmodule

module main_control_circuit (
  input  [6:0] I6_0,
  output MemtoReg,
  output RegWrite,
  output MemRead,
  output MemWrite,
  output Branch
);

  wire not_6_out, not_7_out;

  // NOT_Gate not_1 has open pins: in=I6_0[0], out=open
  // NOT_Gate not_2 has open pins: in=I6_0[1], out=open
  // NOT_Gate not_3 has open pins: in=I6_0[2], out=open
  // NOT_Gate not_4 has open pins: in=I6_0[3], out=open
  not not_5 (MemtoReg, I6_0[4]);
  not not_6 (not_6_out, I6_0[5]);
  not not_7 (not_7_out, I6_0[6]);
  or or_1 (RegWrite, not_6_out, I6_0[4]);
  and and_1 (MemRead, MemtoReg, not_6_out);
  and and_2 (MemWrite, MemtoReg, not_7_out, I6_0[5]);

  assign Branch = I6_0[6];
endmodule

module BitRegister32 (
  input  [31:0] WData,
  input  Write,
  input  [4:0] RReg1,
  input  [4:0] WReg,
  input  [4:0] RReg2,
  input  Clock_in,
  output [31:0] RData1,
  output [31:0] RData2
);

  wire demultiplexer_1_out0, demultiplexer_1_out1, demultiplexer_1_out2, demultiplexer_1_out3,
       demultiplexer_1_out4, demultiplexer_1_out5, demultiplexer_1_out6, demultiplexer_1_out7,
       demultiplexer_1_out8, demultiplexer_1_out9, demultiplexer_1_out10, demultiplexer_1_out11,
       demultiplexer_1_out12, demultiplexer_1_out13, demultiplexer_1_out14, demultiplexer_1_out15,
       demultiplexer_1_out16, demultiplexer_1_out17, demultiplexer_1_out18, demultiplexer_1_out19,
       demultiplexer_1_out20, demultiplexer_1_out21, demultiplexer_1_out22, demultiplexer_1_out23,
       demultiplexer_1_out24, demultiplexer_1_out25, demultiplexer_1_out26, demultiplexer_1_out27,
       demultiplexer_1_out28, demultiplexer_1_out29, demultiplexer_1_out30, demultiplexer_1_out31;
  wire [31:0] register_1_q, register_2_q, register_3_q, register_4_q, register_5_q, register_6_q,
       register_7_q, register_8_q, register_9_q, register_10_q, register_11_q, register_12_q, register_13_q,
       register_14_q, register_15_q, register_16_q, register_17_q, register_18_q, register_19_q,
       register_20_q, register_21_q, register_22_q, register_23_q, register_24_q, register_25_q,
       register_26_q, register_27_q, register_28_q, register_29_q, register_30_q, register_31_q,
       register_32_q;

  Demultiplexer #(.select(5)) demultiplexer_1 (
    .out0(demultiplexer_1_out0), .out1(demultiplexer_1_out1), .out2(demultiplexer_1_out2),
    .out3(demultiplexer_1_out3), .out4(demultiplexer_1_out4), .out5(demultiplexer_1_out5),
    .out6(demultiplexer_1_out6), .out7(demultiplexer_1_out7), .out8(demultiplexer_1_out8),
    .out9(demultiplexer_1_out9), .out10(demultiplexer_1_out10), .out11(demultiplexer_1_out11),
    .out12(demultiplexer_1_out12), .out13(demultiplexer_1_out13), .out14(demultiplexer_1_out14),
    .out15(demultiplexer_1_out15), .out16(demultiplexer_1_out16), .out17(demultiplexer_1_out17),
    .out18(demultiplexer_1_out18), .out19(demultiplexer_1_out19), .out20(demultiplexer_1_out20),
    .out21(demultiplexer_1_out21), .out22(demultiplexer_1_out22), .out23(demultiplexer_1_out23),
    .out24(demultiplexer_1_out24), .out25(demultiplexer_1_out25), .out26(demultiplexer_1_out26),
    .out27(demultiplexer_1_out27), .out28(demultiplexer_1_out28), .out29(demultiplexer_1_out29),
    .out30(demultiplexer_1_out30), .out31(demultiplexer_1_out31), .in(Write), .sel(WReg));
  Register #(.width(32)) register_1 (
    .D(WData), .en(demultiplexer_1_out0), .Q(register_1_q), .clk(Clock_in));  // open: clr
  Register #(.width(32)) register_2 (
    .D(WData), .en(demultiplexer_1_out1), .Q(register_2_q), .clk(Clock_in));  // open: clr
  Register #(.width(32)) register_3 (
    .D(WData), .en(demultiplexer_1_out2), .Q(register_3_q), .clk(Clock_in));  // open: clr
  Register #(.width(32)) register_4 (
    .D(WData), .en(demultiplexer_1_out3), .Q(register_4_q), .clk(Clock_in));  // open: clr
  Register #(.width(32)) register_5 (
    .D(WData), .en(demultiplexer_1_out4), .Q(register_5_q), .clk(Clock_in));  // open: clr
  Register #(.width(32)) register_6 (
    .D(WData), .en(demultiplexer_1_out5), .Q(register_6_q), .clk(Clock_in));  // open: clr
  Register #(.width(32)) register_7 (
    .D(WData), .en(demultiplexer_1_out6), .Q(register_7_q), .clk(Clock_in));  // open: clr
  Register #(.width(32)) register_8 (
    .D(WData), .en(demultiplexer_1_out7), .Q(register_8_q), .clk(Clock_in));  // open: clr
  Register #(.width(32)) register_9 (
    .D(WData), .en(demultiplexer_1_out8), .Q(register_9_q), .clk(Clock_in));  // open: clr
  Register #(.width(32)) register_10 (
    .D(WData), .en(demultiplexer_1_out9), .Q(register_10_q), .clk(Clock_in));  // open: clr
  Register #(.width(32)) register_11 (
    .D(WData), .en(demultiplexer_1_out10), .Q(register_11_q), .clk(Clock_in));  // open: clr
  Register #(.width(32)) register_12 (
    .D(WData), .en(demultiplexer_1_out11), .Q(register_12_q), .clk(Clock_in));  // open: clr
  Register #(.width(32)) register_13 (
    .D(WData), .en(demultiplexer_1_out12), .Q(register_13_q), .clk(Clock_in));  // open: clr
  Register #(.width(32)) register_14 (
    .D(WData), .en(demultiplexer_1_out13), .Q(register_14_q), .clk(Clock_in));  // open: clr
  Register #(.width(32)) register_15 (
    .D(WData), .en(demultiplexer_1_out14), .Q(register_15_q), .clk(Clock_in));  // open: clr
  Register #(.width(32)) register_16 (
    .D(WData), .en(demultiplexer_1_out15), .Q(register_16_q), .clk(Clock_in));  // open: clr
  Register #(.width(32)) register_17 (
    .D(WData), .en(demultiplexer_1_out16), .Q(register_17_q), .clk(Clock_in));  // open: clr
  Register #(.width(32)) register_18 (
    .D(WData), .en(demultiplexer_1_out17), .Q(register_18_q), .clk(Clock_in));  // open: clr
  Register #(.width(32)) register_19 (
    .D(WData), .en(demultiplexer_1_out18), .Q(register_19_q), .clk(Clock_in));  // open: clr
  Register #(.width(32)) register_20 (
    .D(WData), .en(demultiplexer_1_out19), .Q(register_20_q), .clk(Clock_in));  // open: clr
  Register #(.width(32)) register_21 (
    .D(WData), .en(demultiplexer_1_out20), .Q(register_21_q), .clk(Clock_in));  // open: clr
  Register #(.width(32)) register_22 (
    .D(WData), .en(demultiplexer_1_out21), .Q(register_22_q), .clk(Clock_in));  // open: clr
  Register #(.width(32)) register_23 (
    .D(WData), .en(demultiplexer_1_out22), .Q(register_23_q), .clk(Clock_in));  // open: clr
  Register #(.width(32)) register_24 (
    .D(WData), .en(demultiplexer_1_out23), .Q(register_24_q), .clk(Clock_in));  // open: clr
  Register #(.width(32)) register_25 (
    .D(WData), .en(demultiplexer_1_out24), .Q(register_25_q), .clk(Clock_in));  // open: clr
  Register #(.width(32)) register_26 (
    .D(WData), .en(demultiplexer_1_out25), .Q(register_26_q), .clk(Clock_in));  // open: clr
  Register #(.width(32)) register_27 (
    .D(WData), .en(demultiplexer_1_out26), .Q(register_27_q), .clk(Clock_in));  // open: clr
  Register #(.width(32)) register_28 (
    .D(WData), .en(demultiplexer_1_out27), .Q(register_28_q), .clk(Clock_in));  // open: clr
  Register #(.width(32)) register_29 (
    .D(WData), .en(demultiplexer_1_out28), .Q(register_29_q), .clk(Clock_in));  // open: clr
  Register #(.width(32)) register_30 (
    .D(WData), .en(demultiplexer_1_out29), .Q(register_30_q), .clk(Clock_in));  // open: clr
  Register #(.width(32)) register_31 (
    .D(WData), .en(demultiplexer_1_out30), .Q(register_31_q), .clk(Clock_in));  // open: clr
  Register #(.width(32)) register_32 (
    .D(WData), .en(demultiplexer_1_out31), .Q(register_32_q), .clk(Clock_in));  // open: clr
  Multiplexer #(.disabled("Z"), .select(5), .width(32)) multiplexer_1 (
    .in0(register_1_q), .in1(register_2_q), .in2(register_3_q), .in3(register_4_q), .in4(register_5_q),
    .in5(register_6_q), .in6(register_7_q), .in7(register_8_q), .in8(register_9_q), .in9(register_10_q),
    .in10(register_11_q), .in11(register_12_q), .in12(register_13_q), .in13(register_14_q),
    .in14(register_15_q), .in15(register_16_q), .in16(register_17_q), .in17(register_18_q),
    .in18(register_19_q), .in19(register_20_q), .in20(register_21_q), .in21(register_22_q),
    .in22(register_23_q), .in23(register_24_q), .in24(register_25_q), .in25(register_26_q),
    .in26(register_27_q), .in27(register_28_q), .in28(register_29_q), .in29(register_30_q),
    .in30(register_31_q), .in31(register_32_q), .out(RData1), .sel(RReg1));
  Multiplexer #(.disabled("Z"), .select(5), .width(32)) multiplexer_2 (
    .in0(register_1_q), .in1(register_2_q), .in2(register_3_q), .in3(register_4_q), .in4(register_5_q),
    .in5(register_6_q), .in6(register_7_q), .in7(register_8_q), .in8(register_9_q), .in9(register_10_q),
    .in10(register_11_q), .in11(register_12_q), .in12(register_13_q), .in13(register_14_q),
    .in14(register_15_q), .in15(register_16_q), .in16(register_17_q), .in17(register_18_q),
    .in18(register_19_q), .in19(register_20_q), .in20(register_21_q), .in21(register_22_q),
    .in22(register_23_q), .in23(register_24_q), .in24(register_25_q), .in25(register_26_q),
    .in26(register_27_q), .in27(register_28_q), .in28(register_29_q), .in29(register_30_q),
    .in30(register_31_q), .in31(register_32_q), .out(RData2), .sel(RReg2));
endmodule

module DRAM64Mx32Byte (
  input  C_in,
  input  OutputEnable,
  input  WriteEnable,
  input  [25:0] Address,
  input  [7:0] DataIn,
  output [7:0] DataOut
);

  wire decoder_1_out0, decoder_2_out0;
  wire [7:0] ram_1_dout, ram_2_dout, ram_3_dout, ram_4_dout;
  wire [23:16] undriven_2;
  wire [31:26] undriven;

  Decoder #(.select(2)) decoder_1 (
    .out0(decoder_1_out0), .out1(decoder_1_out0), .out2(decoder_1_out0), .out3(decoder_1_out0),
    .sel(Address[1:0]), .en(OutputEnable));
  Decoder #(.select(2)) decoder_2 (
    .out0(decoder_2_out0), .out1(decoder_2_out0), .out2(decoder_2_out0), .out3(decoder_2_out0),
    .sel(Address[1:0]), .en(WriteEnable));
  RAM #(.addrWidth(24)) ram_1 (
    .addr({undriven_2, undriven[27], Address[17:3]}), .we(decoder_2_out0), .oe(decoder_1_out0), .clk(C_in),
    .din(DataIn), .dout(ram_1_dout));
  RAM #(.addrWidth(24)) ram_2 (
    .addr({undriven_2, undriven[27], Address[17:3]}), .we(decoder_2_out0), .oe(decoder_1_out0), .clk(C_in),
    .din(DataIn), .dout(ram_2_dout));
  RAM #(.addrWidth(24)) ram_3 (
    .addr({undriven_2, undriven[27], Address[17:3]}), .we(decoder_2_out0), .oe(decoder_1_out0), .clk(C_in),
    .din(DataIn), .dout(ram_3_dout));
  RAM #(.addrWidth(24)) ram_4 (
    .addr({undriven_2, undriven[27], Address[17:3]}), .we(decoder_2_out0), .oe(decoder_1_out0), .clk(C_in),
    .din(DataIn), .dout(ram_4_dout));
  Multiplexer #(.select(2), .width(8)) multiplexer_1 (
    .in0(ram_1_dout), .in1(ram_2_dout), .in2(ram_3_dout), .in3(ram_4_dout), .out(DataOut), .sel(Address[1:0]));
  // Pins of 26 and 32 bits meet at {undriven, Address}
  // Pins of 16 and 24 bits meet at {undriven_2, undriven[27], Address[17:3]}
  // Pins of 2 and 15 bits meet at {undriven[31:28], undriven[26], Address[25:18], Address[1:0]}
endmodule

module task_4_completed_circuit (
  input  [31:0] Instruction
);

  wire alucontrolcircuit_1_alu_src, clock_1_out;
  wire [3:0] alucontrolcircuit_1_alu_ctrl0;
  wire [31:0] bit_extender_1_out, bitregister32_1_rdata1, bitregister32_1_rdata2, multiplexer_1_out,
       thirty_two_bit_alu_1_r;

  Clock clock_1 (.out(clock_1_out));
  assign bit_extender_1_out = {{20{Instruction[31]}}, Instruction[31:20]};  // Bit_Extender bit_extender_1
  ALUControlCircuit alucontrolcircuit_1 (
    .I30(Instruction[30]), .I14(Instruction[14]), .I13(Instruction[13]), .I12(Instruction[12]),
    .I5(Instruction[5]), .I4(Instruction[4]), .ALU_Ctrl3(alucontrolcircuit_1_alu_ctrl0[3]),
    .ALU_Ctrl2(alucontrolcircuit_1_alu_ctrl0[2]), .ALU_Ctrl1(alucontrolcircuit_1_alu_ctrl0[1]),
    .ALU_Ctrl0(alucontrolcircuit_1_alu_ctrl0[0]), .ALU_Src(alucontrolcircuit_1_alu_src));
  BitRegister32 bitregister32_1 (
    .WData(thirty_two_bit_alu_1_r), .Write(1'b1), .RReg1(Instruction[19:15]), .WReg(Instruction[11:7]),
    .RReg2(Instruction[24:20]), .Clock_in(clock_1_out), .RData1(bitregister32_1_rdata1),
    .RData2(bitregister32_1_rdata2));
  Multiplexer #(.width(32)) multiplexer_1 (
    .in0(bitregister32_1_rdata2), .in1(bit_extender_1_out), .out(multiplexer_1_out),
    .sel(alucontrolcircuit_1_alu_src));
  thirty_two_bit_ALU thirty_two_bit_alu_1 (
    .ALU_Ctrl(alucontrolcircuit_1_alu_ctrl0), .A(bitregister32_1_rdata1), .B(multiplexer_1_out),
    .R(thirty_two_bit_alu_1_r));  // open: C_in, C_out
endmodule
